# Fritzing sketch Untitled Sketch 6_Commun_cathode (saved by Fritzing 0.9.6b)
circuit board: 5.46864cm x 3.50661cm
breadboards: 1

parts:
  VCC1 = Battery block 9V
  R4 = Resistor [tolerance=±5% power=0.25 resistance=220 package=THT]
  R2 = Resistor [tolerance=±5% power=0.25 resistance=220 package=THT]
  R5 = Resistor [tolerance=±5% power=0.25 resistance=220 package=THT]
  R3 = Resistor [tolerance=±5% power=0.25 resistance=220 package=THT]
  R6 = Resistor [tolerance=±5% power=0.25 resistance=220 package=THT]
  R1 = Resistor [tolerance=±5% power=0.25 resistance=220 package=THT]
  S3 = Toggle Switch [package=THT]
  S1 = Toggle Switch [package=THT]
  S2 = Toggle Switch [package=THT]
  LED1 = LED - 5mm [color="Red (633nm)" current=0.030 package="5 mm [THT]"]
  LED3 = LED - 5mm [color="Red (633nm)" current=0.030 package="5 mm [THT]"]
  LED2 = LED - 5mm [color="Red (633nm)" current=0.030 package="5 mm [THT]"]
  LEDRGB = RGB LED (com. cathode, rgb) [package="5 mm [THT]"]
  R7 = Resistor [tolerance=±5% power=0.25 resistance=220 package=THT]

nets:
  N1: VCC1.-, R5.Pin_1, R1.Pin_0
  GND: VCC1.+, R4.Pin_1, LED3.cathode, LED2.cathode, LEDRGB.common_cathode
  N2: R4.Pin_0, R2.Pin_0, R3.Pin_0, LED1.cathode
  N3: R2.Pin_1, S2.COM
  N4: R5.Pin_0, LEDRGB.red_anode
  N5: R3.Pin_1, S3.COM
  N6: R6.Pin_0, LEDRGB.green_anode
  N7: R6.Pin_1, S2.L2, LED2.anode
  N8: R1.Pin_1, S1.COM
  N9: S3.L2, LED3.anode, R7.Pin_1
  N10: S1.L2, LED1.anode
  N11: LEDRGB.blue_anode, R7.Pin_0

notes:
  Soutien Academique Tech
  Version B
