# Fritzing sketch Untitled Sketch Commun_anode (saved by Fritzing 0.9.6b)
circuit board: 5.57285cm x 3.4159cm
breadboards: 1

parts:
  R2 = Resistor [tolerance=±5% power=0.25 resistance=220 package=THT]
  R1 = Resistor [tolerance=±5% power=0.25 resistance=220 package=THT]
  VCC = Battery block 9V
  LED1 = LED - 5mm [color="Red (633nm)" current=0.030 package="5 mm [THT]"]
  LED2 = LED - 5mm [color="Red (633nm)" current=0.030 package="5 mm [THT]"]
  S2 = Toggle Switch [package=THT]
  R3 = Resistor [tolerance=±5% power=0.25 resistance=220 package=THT]
  S3 = Toggle Switch [package=THT]
  LED3 = LED - 5mm [color="Red (633nm)" current=0.030 package="5 mm [THT]"]
  R4 = Resistor [tolerance=±5% power=0.25 resistance=220 package=THT]
  R5 = Resistor [tolerance=±5% power=0.25 resistance=220 package=THT]
  R6 = Resistor [tolerance=±5% power=0.25 resistance=220 package=THT]
  R7 = Resistor [tolerance=±5% power=0.25 resistance=220 package=THT]
  S1 = Toggle Switch [package=THT]
  LEDRBG = RGB LED - (4 legs) [package="5 mm [THT]"]

nets:
  N1: R2.Pin_0, LED1.cathode, R3.Pin_0, R4.Pin_0
  N2: R2.Pin_1, S2.COM
  N3: R1.Pin_0, VCC.-, LEDRBG.common_anode
  N4: R1.Pin_1, S1.COM
  GND: VCC.+, LED2.cathode, LED3.cathode, R4.Pin_1, R5.Pin_1
  N5: LED1.anode, S1.L2
  N6: LED2.anode, S2.L2, R6.Pin_1
  N7: R3.Pin_1, S3.COM
  N8: S3.L2, LED3.anode, R7.Pin_1
  N9: R5.Pin_0, LEDRBG.red_cathode
  N10: R6.Pin_0, LEDRBG.green_cathode
  N11: R7.Pin_0, LEDRBG.blue_cathode

notes:
  Soutien Academique Tech
  Version A
